// Logisim project tta8_opt.circ as structural Verilog: 1 circuit, main circuit main
module main (
  input  in_1
);

  wire AeB0, AeB1, and_1_out, and_2_out, and_3_out, and_4_out, and_5_out, and_6_out, and_7_out, and_8_out,
       and_9_out, and_10_out, and_11_out, and_12_out, and_13_out, and_14_out, and_15_out, and_16_out,
       and_17_out, and_18_out, and_19_out, and_20_out, and_21_out, and_22_out, and_23_out, and_25_out,
       and_26_out, and_27_out, and_28_out, and_30_out, and_31_out, and_32_out, and_33_out, and_34_out,
       and_35_out, and_36_out, and_37_out, and_38_out, and_39_out, and_40_out, and_41_out, and_42_out,
       and_43_out, and_44_out, and_45_out, and_46_out, and_47_out, and_48_out, and_49_out, and_50_out,
       and_51_out, and_53_out, and_54_out, and_55_out, and_56_out, and_57_out, and_58_out, and_59_out,
       and_60_out, and_61_out, and_62_out, and_63_out, and_64_out, and_65_out, and_66_out, and_67_out,
       and_68_out, and_69_out, and_70_out, and_71_out, and_72_out, and_73_out, and_74_out, and_75_out,
       and_76_out, and_77_out, and_78_out, and_79_out, and_80_out, and_81_out, and_82_out, and_83_out,
       and_84_out, and_85_out, and_86_out, and_87_out, and_88_out, and_89_out, and_90_out, and_91_out,
       and_92_out, and_93_out, and_94_out, and_95_out, and_96_out, and_97_out, and_98_out, and_99_out,
       and_100_out, and_101_out, and_102_out, and_103_out, and_104_out, and_105_out, and_106_out,
       and_107_out, and_108_out, and_109_out, C, CARRY, cef, cen, Cn, Cn4_0, Cn4_1, CnX, CnY, CnZ,
       decoder_4_out0, decoder_4_out1, decoder_4_out2, decoder_4_out3, EXC, G, G0, G1, LDI, m, MOV, mv, mvc,
       MVI, mvz, nand_1_out, nand_2_out, nand_3_out, nand_5_out, nand_6_out, nand_7_out, nand_9_out,
       nand_11_out, nor_1_out, nor_2_out, nor_3_out, nor_4_out, nor_6_out, nor_7_out, nor_9_out, nor_10_out,
       nor_11_out, nor_12_out, nor_14_out, nor_15_out, nor_16_out, nor_17_out, nor_18_out, nor_19_out,
       nor_21_out, nor_22_out, nor_23_out, nor_24_out, nor_25_out, nor_26_out, nor_27_out, nor_28_out,
       nor_29_out, nor_31_out, not_1_out, not_2_out, not_3_out, not_4_out, not_5_out, not_6_out, not_7_out,
       not_8_out, not_9_out, not_10_out, not_11_out, not_12_out, not_13_out, not_14_out, not_15_out,
       not_16_out, not_17_out, not_18_out, not_19_out, not_20_out, not_21_out, or_1_out, or_2_out, P, P0, P1,
       R, R_al, RD, s0, s1, s2, s3, WR, ZERO;
  wire [2:0] DSTE, mvidata;
  wire [3:0] dipswitch_1_sw4, dipswitch_1_sw8, nH, nL, register_3_q, register_4_q, register_5_q, register_6_q;
  wire [7:0] a, Acc_q, alu, b, DATA, dipswitch_2_sw8, DST, SRC, undriven;
  wire [7:6] register_1_q;
  wire [7:7] Control_q;
  wire [15:0] ADDRESS, counter_1_q, register_2_q, T_BUS;

  nand nand_1 (nand_1_out, DST[1], MOV);
  nand nand_2 (nand_2_out, Cn, not_2_out);
  nand nand_3 (nand_3_out, CnX, not_3_out);
  not not_1 (not_1_out, Cn);
  D_Flip_Flop d_ff_1 (.D(LDI), .clk(C), .Q(EXC), .Qn(LDI), .reset(R));  // open: preset
  Register #(.trigger("high")) register_1 (.D(DATA), .en(1'b1), .clk(LDI), .Q({register_1_q, DSTE, mvidata}), .clr(R));
  Register #(.trigger("low"), .width(16)) register_2 (
    .D(T_BUS), .en(1'b1), .clk(nand_1_out), .Q(register_2_q), .clr(R));
  not not_2 (not_2_out, m);
  and and_1 (and_1_out, a[0], a[0]);
  xor xor_1 (alu[0], nand_2_out, and_8_out);
  not not_3 (not_3_out, m);
  and and_2 (and_2_out, a[4], a[4]);
  xor xor_2 (alu[4], nand_3_out, and_12_out);
  and and_3 (and_3_out, G0, P0);
  Decoder #(.enable("false"), .select(2)) decoder_1 (.out0(mv), .out1(mvc), .out2(mvz), .out3(MVI), .sel(register_1_q));
  assign T_BUS = and_4_out ? register_2_q : 16'bz;  // Controlled_Buffer controlled_buffer_1
  and and_4 (and_4_out, SRC[1], MOV);
  assign ADDRESS = or_1_out ? register_2_q : 16'bz;  // Controlled_Buffer controlled_buffer_2
  or or_1 (or_1_out, and_35_out, and_36_out);
  and and_5 (and_5_out, b[0], s0);
  and and_6 (and_6_out, s1, not_6_out);
  nor nor_1 (nor_1_out, and_1_out, and_5_out, and_6_out);
  not not_4 (not_4_out, nor_1_out);
  and and_7 (and_7_out, not_2_out, nor_1_out);
  and and_8 (and_8_out, not_4_out, nor_6_out);
  nor nor_2 (nor_2_out, and_7_out, and_15_out);
  and and_9 (and_9_out, b[4], s0);
  and and_10 (and_10_out, s1, not_7_out);
  nor nor_3 (nor_3_out, and_2_out, and_9_out, and_10_out);
  not not_5 (not_5_out, nor_3_out);
  and and_11 (and_11_out, not_3_out, nor_3_out);
  and and_12 (and_12_out, not_5_out, nor_7_out);
  nor nor_4 (nor_4_out, and_11_out, and_17_out);
  and and_13 (and_13_out, not_1_out, G0);
  nor nor_5 (CnX, and_3_out, and_13_out);
  not not_6 (not_6_out, b[0]);
  and and_14 (and_14_out, not_6_out, s2, a[0]);
  nor nor_6 (nor_6_out, and_14_out, and_20_out);
  and and_15 (and_15_out, not_2_out, nor_6_out, Cn);
  xor xor_3 (alu[1], nor_2_out, and_23_out);
  not not_7 (not_7_out, b[4]);
  and and_16 (and_16_out, not_7_out, s2, a[4]);
  nor nor_7 (nor_7_out, and_16_out, and_25_out);
  and and_17 (and_17_out, not_3_out, nor_7_out, CnX);
  xor xor_4 (alu[5], nor_4_out, and_28_out);
  and and_18 (and_18_out, G1, P1);
  and and_19 (and_19_out, G0, G1, P0);
  nor nor_8 (CnY, and_18_out, and_19_out, and_30_out);
  nand nand_4 (R, R_al, R_al);
  Decoder #(.enable("false"), .select(3)) decoder_2 (
    .out0(DST[0]), .out1(DST[1]), .out2(DST[2]), .out3(DST[3]), .out4(DST[4]), .out5(DST[5]), .out6(DST[6]),
    .out7(DST[7]), .sel(DSTE));
  and and_20 (and_20_out, a[0], b[0], s3);
  and and_21 (and_21_out, a[1], a[1]);
  not not_8 (not_8_out, nor_9_out);
  and and_22 (and_22_out, not_2_out, nor_9_out);
  and and_23 (and_23_out, not_8_out, nor_14_out);
  and and_24 (AeB0, alu[0], alu[1], alu[2], alu[3]);
  and and_25 (and_25_out, a[4], b[4], s3);
  and and_26 (and_26_out, a[5], a[5]);
  not not_9 (not_9_out, nor_11_out);
  and and_27 (and_27_out, not_3_out, nor_11_out);
  and and_28 (and_28_out, not_9_out, nor_15_out);
  and and_29 (AeB1, alu[4], alu[5], alu[6], alu[7]);
  and and_30 (and_30_out, not_1_out, G0, G1);
  and and_31 (and_31_out, 1'b0, 1'b0);
  and and_32 (and_32_out, CARRY, mvc);
  and and_33 (and_33_out, ZERO, mvz);
  and and_34 (and_34_out, MOV, DST[0]);
  Decoder #(.enable("false"), .select(3)) decoder_3 (
    .out0(SRC[0]), .out1(SRC[1]), .out2(SRC[2]), .out3(SRC[3]), .out4(SRC[4]), .out5(SRC[5]), .out6(SRC[6]),
    .out7(SRC[7]), .sel(mvidata));
  assign DATA = and_35_out ? T_BUS[7:0] : 8'bz;  // Controlled_Buffer controlled_buffer_3
  and and_35 (and_35_out, DST[2], MOV);
  assign T_BUS[7:0] = and_36_out ? DATA : 8'bz;  // Controlled_Buffer controlled_buffer_4
  and and_36 (and_36_out, SRC[2], MOV);
  and and_37 (and_37_out, b[1], s0);
  nor nor_9 (nor_9_out, and_21_out, and_37_out, and_43_out);
  and and_38 (and_38_out, not_2_out, nor_1_out, nor_14_out);
  nor nor_10 (nor_10_out, and_22_out, and_38_out, and_45_out);
  xor xor_5 (alu[2], nor_10_out, and_46_out);
  and and_39 (and_39_out, b[5], s0);
  nor nor_11 (nor_11_out, and_26_out, and_39_out, and_47_out);
  and and_40 (and_40_out, not_3_out, nor_3_out, nor_15_out);
  nor nor_12 (nor_12_out, and_27_out, and_40_out, and_49_out);
  xor xor_6 (alu[6], nor_12_out, and_50_out);
  and and_41 (and_41_out, G1, 1'b0, P1);
  and and_42 (and_42_out, G0, G1, 1'b0, P0);
  nor nor_13 (CnZ, and_31_out, and_41_out, and_42_out, and_51_out);
  or or_2 (or_2_out, and_32_out, and_33_out, mv);
  Counter #(.max('hffff), .width(16)) counter_1 (
    .load(and_34_out), .D(T_BUS), .count(1'b1), .Q(counter_1_q), .up(1'b1), .clk(LDI), .clr(R));  // open: carry
  not not_10 (not_10_out, b[1]);
  and and_43 (and_43_out, s1, not_10_out);
  and and_44 (and_44_out, not_10_out, s2, a[1]);
  not not_11 (not_11_out, nor_16_out);
  and and_45 (and_45_out, not_2_out, Cn, nor_6_out, nor_14_out);
  and and_46 (and_46_out, not_11_out, nor_21_out);
  not not_12 (not_12_out, b[5]);
  and and_47 (and_47_out, s1, not_12_out);
  and and_48 (and_48_out, not_12_out, s2, a[5]);
  not not_13 (not_13_out, nor_18_out);
  and and_49 (and_49_out, not_3_out, CnX, nor_7_out, nor_15_out);
  and and_50 (and_50_out, not_13_out, nor_22_out);
  and and_51 (and_51_out, not_1_out, G0, G1, 1'b0);
  and and_52 (MOV, or_2_out, EXC);
  assign ADDRESS = and_53_out ? counter_1_q : 16'bz;  // Controlled_Buffer controlled_buffer_5
  and and_53 (and_53_out, LDI, LDI);
  assign T_BUS = and_54_out ? {16{1'b0}} : 16'bz;  // Controlled_Buffer controlled_buffer_6
  and and_54 (and_54_out, SRC[0], MOV);
  and and_55 (and_55_out, a[1], s3, b[1]);
  nor nor_14 (nor_14_out, and_44_out, and_55_out);
  and and_56 (and_56_out, not_2_out, nor_16_out);
  and and_57 (and_57_out, a[5], s3, b[5]);
  nor nor_15 (nor_15_out, and_48_out, and_57_out);
  and and_58 (and_58_out, not_3_out, nor_18_out);
  and and_59 (and_59_out, 1'b0, 1'b0);
  Register #(.trigger("low")) u_A (.D(T_BUS[7:0]), .en(1'b1), .clk(nand_5_out), .Q(a), .clr(R));
  nand nand_5 (nand_5_out, MOV, DST[3]);
  Register #(.trigger("low")) u_B (.D(T_BUS[7:0]), .en(1'b1), .clk(nand_6_out), .Q(b), .clr(R));
  nand nand_6 (nand_6_out, MOV, DST[4]);
  and and_60 (and_60_out, a[2], a[2]);
  and and_61 (and_61_out, b[2], s0);
  nor nor_16 (nor_16_out, and_60_out, and_61_out, and_72_out);
  and and_62 (and_62_out, not_2_out, nor_9_out, nor_21_out);
  and and_63 (and_63_out, not_2_out, nor_1_out, nor_14_out, nor_21_out);
  nor nor_17 (nor_17_out, and_56_out, and_62_out, and_63_out, and_73_out);
  xor xor_7 (alu[3], nor_17_out, and_80_out);
  and and_64 (and_64_out, a[6], a[6]);
  and and_65 (and_65_out, b[6], s0);
  nor nor_18 (nor_18_out, and_64_out, and_65_out, and_74_out);
  and and_66 (and_66_out, not_3_out, nor_11_out, nor_22_out);
  and and_67 (and_67_out, not_3_out, nor_3_out, nor_15_out, nor_22_out);
  nor nor_19 (nor_19_out, and_58_out, and_66_out, and_67_out, and_75_out);
  xor xor_8 (alu[7], nor_19_out, and_83_out);
  and and_68 (and_68_out, 1'b0, 1'b0, 1'b0);
  and and_69 (and_69_out, G1, 1'b0, 1'b0, P1);
  nor nor_20 (G, and_59_out, and_68_out, and_69_out, and_76_out);
  Multiplexer #(.disabled("Z"), .width(8)) multiplexer_1 (
    .in0(T_BUS[7:0]), .in1({DSTE[0], mvidata, DSTE[0], mvidata}), .out({nH, nL}), .sel(MVI));
  assign T_BUS[7:0] = and_70_out ? a : 8'bz;  // Controlled_Buffer controlled_buffer_7
  and and_70 (and_70_out, SRC[3], MOV);
  assign T_BUS[7:0] = and_71_out ? b : 8'bz;  // Controlled_Buffer controlled_buffer_8
  and and_71 (and_71_out, SRC[4], MOV);
  not not_14 (not_14_out, b[2]);
  and and_72 (and_72_out, s1, not_14_out);
  and and_73 (and_73_out, not_2_out, Cn, nor_6_out, nor_14_out, nor_21_out);
  not not_15 (not_15_out, b[6]);
  and and_74 (and_74_out, s1, not_15_out);
  and and_75 (and_75_out, not_3_out, CnX, nor_7_out, nor_15_out, nor_22_out);
  and and_76 (and_76_out, G0, G1, 1'b0, 1'b0);
  and and_77 (and_77_out, EXC, MVI);
  Decoder #(.select(2)) decoder_4 (
    .out0(decoder_4_out0), .out1(decoder_4_out1), .out2(decoder_4_out2), .out3(decoder_4_out3),
    .sel(DSTE[2:1]), .en(and_77_out));
  and and_78 (and_78_out, not_14_out, s2, a[2]);
  and and_79 (and_79_out, a[2], s3, b[2]);
  nor nor_21 (nor_21_out, and_78_out, and_79_out);
  not not_16 (not_16_out, nor_23_out);
  and and_80 (and_80_out, not_16_out, nor_29_out);
  and and_81 (and_81_out, not_15_out, s2, a[6]);
  and and_82 (and_82_out, a[6], s3, b[6]);
  nor nor_22 (nor_22_out, and_81_out, and_82_out);
  not not_17 (not_17_out, nor_24_out);
  and and_83 (and_83_out, not_17_out, nor_31_out);
  or or_3 (P, P0, P1, 1'b0, 1'b0);
  Register #(.trigger("low")) Control (
    .D(T_BUS[7:0]), .en(1'b1), .clk(nand_7_out), .Q({Control_q[7], cef, cen, m, s3, s2, s1, s0}), .clr(R));
  nand nand_7 (nand_7_out, MOV, DST[5]);
  Register #(.trigger("low")) Acc (.D(alu), .en(1'b1), .clk(EXC), .Q(Acc_q), .clr(R));
  and and_84 (and_84_out, a[3], a[3]);
  nand nand_8 (P0, nor_6_out, nor_14_out, nor_21_out, nor_29_out);
  nand nand_9 (nand_9_out, Cn, nor_6_out, nor_14_out, nor_21_out, nor_29_out);
  or or_4 (Cn4_0, ~nand_9_out, ~G0);  // OR_Gate
  and and_85 (and_85_out, a[7], a[7]);
  nand nand_10 (P1, nor_7_out, nor_15_out, nor_22_out, nor_31_out);
  nand nand_11 (nand_11_out, CnX, nor_7_out, nor_15_out, nor_22_out, nor_31_out);
  or or_5 (Cn4_1, ~nand_11_out, ~G1);  // OR_Gate
  and and_86 (and_86_out, MOV, DST[6]);
  and and_87 (and_87_out, MOV, DST[7]);
  assign T_BUS[7:0] = and_88_out ? Acc_q : 8'bz;  // Controlled_Buffer controlled_buffer_9
  and and_88 (and_88_out, SRC[5], MOV);
  and and_89 (and_89_out, s1, not_18_out);
  and and_90 (and_90_out, b[3], s0);
  nor nor_23 (nor_23_out, and_84_out, and_90_out, and_89_out);
  and and_91 (and_91_out, nor_1_out, nor_14_out, nor_21_out, nor_29_out);
  and and_92 (and_92_out, s1, not_19_out);
  and and_93 (and_93_out, b[7], s0);
  nor nor_24 (nor_24_out, and_85_out, and_93_out, and_92_out);
  and and_94 (and_94_out, nor_3_out, nor_15_out, nor_22_out, nor_31_out);
  nor nor_25 (nor_25_out, and_86_out, decoder_4_out0);
  nor nor_26 (nor_26_out, and_86_out, decoder_4_out1);
  nor nor_27 (nor_27_out, and_87_out, decoder_4_out2);
  nor nor_28 (nor_28_out, and_87_out, decoder_4_out3);
  not not_18 (not_18_out, b[3]);
  and and_95 (and_95_out, not_18_out, s2, a[3]);
  and and_96 (and_96_out, a[3], s3, b[3]);
  nor nor_29 (nor_29_out, and_95_out, and_96_out);
  and and_97 (and_97_out, nor_9_out, nor_21_out, nor_29_out);
  and and_98 (and_98_out, nor_16_out, nor_29_out);
  nor nor_30 (G0, and_91_out, and_97_out, and_98_out, and_103_out);
  not not_19 (not_19_out, b[7]);
  and and_99 (and_99_out, not_19_out, s2, a[7]);
  and and_100 (and_100_out, a[7], s3, b[7]);
  nor nor_31 (nor_31_out, and_99_out, and_100_out);
  and and_101 (and_101_out, nor_11_out, nor_22_out, nor_31_out);
  and and_102 (and_102_out, nor_18_out, nor_31_out);
  nor nor_32 (G1, and_94_out, and_101_out, and_102_out, and_104_out);
  Register #(.trigger("low"), .width(4)) register_3 (.D(nL), .en(1'b1), .clk(nor_25_out), .Q(register_3_q), .clr(R));
  Register #(.trigger("low"), .width(4)) register_4 (.D(nH), .en(1'b1), .clk(nor_26_out), .Q(register_4_q), .clr(R));
  Register #(.trigger("low"), .width(4)) register_5 (.D(nL), .en(1'b1), .clk(nor_27_out), .Q(register_5_q), .clr(R));
  Register #(.trigger("low"), .width(4)) register_6 (.D(nH), .en(1'b1), .clk(nor_28_out), .Q(register_6_q), .clr(R));
  Comparator #(.mode("unsigned")) comparator_1 (.a(alu), .b({8{1'b0}}), .eq(ZERO));  // open: gt, lt
  and and_103 (and_103_out, nor_23_out, nor_23_out);
  and and_104 (and_104_out, nor_24_out, nor_24_out);
  and and_105 (and_105_out, SRC[6], MOV);
  and and_106 (and_106_out, SRC[7], MOV);
  D_Flip_Flop d_ff_2 (.D(CnY), .clk(LDI), .Qn(CARRY));  // open: Q, preset, reset
  assign T_BUS = and_105_out ? {register_6_q, register_5_q, register_4_q, register_3_q} : 16'bz;  // Controlled_Buffer controlled_buffer_10
  assign T_BUS = and_106_out ? {{8{1'b0}}, register_6_q, register_5_q} : 16'bz;  // Controlled_Buffer controlled_buffer_11
  // LedBar #(.inputtype("row")) ledbar_1: pin names not known; wires that end beside it: a
  // LedBar #(.inputtype("row")) ledbar_2: pin names not known; wires that end beside it: b
  // LedBar #(.inputtype("row")) ledbar_3: pin names not known; wires that end beside it: alu
  Hex_Digit_Display #(.decimalPoint("false")) hex_digit_display_1 (.value(T_BUS[15:12]));
  Hex_Digit_Display #(.decimalPoint("false")) hex_digit_display_2 (.value(T_BUS[11:8]));
  Hex_Digit_Display #(.decimalPoint("false")) hex_digit_display_3 (.value(dipswitch_1_sw4));
  DipSwitch dipswitch_1 (
    .sw1(dipswitch_1_sw4[3]), .sw2(dipswitch_1_sw4[2]), .sw3(dipswitch_1_sw4[1]), .sw4(dipswitch_1_sw4[0]),
    .sw5(dipswitch_1_sw8[3]), .sw6(dipswitch_1_sw8[2]), .sw7(dipswitch_1_sw8[1]), .sw8(dipswitch_1_sw8[0]));
  RAM #(.addrWidth(16), .databus("bidir"), .trigger("high")) ram_1 (
    .addr(ADDRESS), .we(not_20_out), .oe(not_21_out));  // open: clk, data
  not not_20 (not_20_out, WR);
  not not_21 (not_21_out, RD);
  and and_107 (and_107_out, cen, CnY);
  or or_6 (Cn, cef, and_107_out);
  Hex_Digit_Display #(.decimalPoint("false")) hex_digit_display_4 (.value(T_BUS[7:4]));
  Hex_Digit_Display #(.decimalPoint("false")) hex_digit_display_5 (.value(T_BUS[3:0]));
  Hex_Digit_Display #(.decimalPoint("false")) hex_digit_display_6 (.value(dipswitch_1_sw8));
  Hex_Digit_Display #(.decimalPoint("false")) hex_digit_display_7 (.value(a[7:4]));
  Hex_Digit_Display #(.decimalPoint("false")) hex_digit_display_8 (.value(b[7:4]));
  Hex_Digit_Display #(.decimalPoint("false")) hex_digit_display_9 (.value(alu[7:4]));
  Hex_Digit_Display #(.decimalPoint("false")) hex_digit_display_10 (.value(ADDRESS[15:12]));
  Clock clock_1 (.out(C));
  Button #(.press("passive")) button_1 (.out(R_al));
  and and_108 (and_108_out, MOV, SRC[2]);
  and and_109 (and_109_out, MOV, DST[2]);
  Pull_Resistor pull_resistor_1 (.node(T_BUS[15]));
  Pull_Resistor pull_resistor_2 (.node(T_BUS[14]));
  Pull_Resistor pull_resistor_3 (.node(T_BUS[13]));
  Pull_Resistor pull_resistor_4 (.node(T_BUS[12]));
  Pull_Resistor pull_resistor_5 (.node(T_BUS[11]));
  Pull_Resistor pull_resistor_6 (.node(T_BUS[10]));
  Pull_Resistor pull_resistor_7 (.node(T_BUS[9]));
  Hex_Digit_Display #(.decimalPoint("false")) hex_digit_display_11 (.value(a[3:0]));
  Hex_Digit_Display #(.decimalPoint("false")) hex_digit_display_12 (.value(b[3:0]));
  Hex_Digit_Display #(.decimalPoint("false")) hex_digit_display_13 (.value(alu[3:0]));
  Hex_Digit_Display #(.decimalPoint("false")) hex_digit_display_14 (.value(ADDRESS[11:8]));
  Hex_Digit_Display #(.decimalPoint("false")) hex_digit_display_15 (.value(ADDRESS[7:4]));
  Hex_Digit_Display #(.decimalPoint("false")) hex_digit_display_16 (.value(DATA[7:4]));
  nor nor_33 (RD, LDI, and_108_out);
  nor nor_34 (WR, and_109_out, and_109_out);
  Pull_Resistor pull_resistor_8 (.node(T_BUS[8]));
  Hex_Digit_Display #(.decimalPoint("false")) hex_digit_display_17 (.value(ADDRESS[3:0]));
  Hex_Digit_Display #(.decimalPoint("false")) hex_digit_display_18 (.value(DATA[3:0]));
  Multiplexer #(.width(8)) multiplexer_2 (.in0(undriven), .in1(dipswitch_2_sw8), .out(DATA), .sel(in_1));
  DipSwitch dipswitch_2 (
    .sw1(dipswitch_2_sw8[7]), .sw2(dipswitch_2_sw8[6]), .sw3(dipswitch_2_sw8[5]), .sw4(dipswitch_2_sw8[4]),
    .sw5(dipswitch_2_sw8[3]), .sw6(dipswitch_2_sw8[2]), .sw7(dipswitch_2_sw8[1]), .sw8(dipswitch_2_sw8[0]));

  // Other names for the same wires on the sheet: SRCE[2:0] = mvidata; mvidata[3] = DSTE[0]; F0 = alu[0]; F1 = alu[1];
  //   F2 = alu[2]; F3 = alu[3]; F4 = alu[4]; F5 = alu[5]; F6 = alu[6]; F7 = alu[7]

  // Notes on the sheet:
  //   dst1
  //   State Machine
  //   Instruction Decoder
  //   Address Pointer
  //   src1
  //   Control Unit
  //   /Reset
  //   Load/Store Unit
  //   dst2
  //   src2
  //   74182
  //   DST 2 (Data Out)
  //   SRC 2 (Data In)
  //   Conditional Logic
  //   Program Counter
  //   Zero Register
  //   DST 3
  //   dst3
  //   DST 4
  //   dst4
  //   74181
  //   74181
  //   Data Splitter
  //   SRC 3
  //   src3
  //   SRC 4
  //   src4
  //   mvi Encoder
  //   ALU Unit
  //   DST 6/7
  //   dst7/6
  //   DST 5
  //   dst5
  //   Register Unit
  //   SRC 5
  //   src5
  //   Registers
  //   SRC 6
  //   src6
  //   SRC 7
  //   src7
  //   Cn Control
  //   Carry Flag
  //   src2
  //   dst2
  //   External Connections
  //   Backplane Logic
  //   R/W Logic
endmodule
